// Logisim project alu.circ as structural Verilog: 1 circuit, main circuit alu
module alu (
  input  [31:0] A,
  input  [31:0] B,
  input  [3:0] ALUSel,
  output [31:0] Result
);

  wire [0:0] slt32;
  wire [31:0] add32, adder_2_out, and32, mul32, mulh32, mulhu32, multiplexer_1_out, multiplexer_2_out,
       negator_1_out, negator_2_out, or32, sll32, sra32, srl32, sub32, xor32;

  Adder #(.width(32)) adder_1 (.a(A), .b(B), .out(add32));  // open: cin, cout
  assign and32 = A & B;  // AND_Gate and_1, 32 bits wide
  assign or32 = A | B;  // OR_Gate or_1, 32 bits wide
  assign xor32 = A ^ B;  // XOR_Gate xor_1, 32 bits wide
  Shifter #(.shift("lr"), .width(32)) shifter_1 (.in(A), .\dist (B[4:0]), .out(srl32));
  Shifter #(.shift("ar"), .width(32)) shifter_2 (.in(A), .\dist (B[4:0]), .out(sra32));
  Shifter #(.width(32)) shifter_3 (.in(A), .\dist (B[4:0]), .out(sll32));
  Comparator #(.width(32)) comparator_1 (.a(A), .b(B), .lt(slt32[0]));  // open: gt, eq
  Multiplier #(.width(32)) multiplier_1 (.a(A), .b(B), .out(mul32), .cout(mulhu32));  // open: cin
  Subtractor #(.width(32)) subtractor_1 (.a(A), .b(B), .out(sub32));  // open: bin, bout
  Negator #(.width(32)) negator_1 (.in(A), .out(negator_1_out));
  Negator #(.width(32)) negator_2 (.in(B), .out(negator_2_out));
  Multiplexer #(.enable("false"), .width(32)) multiplexer_1 (
    .in0({32{1'b0}}), .in1(negator_1_out), .out(multiplexer_1_out), .sel(B[31]));
  Multiplexer #(.enable("false"), .width(32)) multiplexer_2 (
    .in0({32{1'b0}}), .in1(negator_2_out), .out(multiplexer_2_out), .sel(A[31]));
  Adder #(.width(32)) adder_2 (.a(multiplexer_1_out), .b(multiplexer_2_out), .out(adder_2_out));  // open: cin, cout
  Adder #(.width(32)) adder_3 (.a(mulhu32), .b(adder_2_out), .out(mulh32));  // open: cin, cout
  Multiplexer #(.enable("false"), .select(4), .width(32)) multiplexer_3 (
    .in0(add32), .in1(and32), .in2(or32), .in3(xor32), .in4(srl32), .in5(sra32), .in6(sll32),
    .in7({{31{1'b0}}, slt32[0]}), .in10(mul32), .in11(mulhu32), .in12(sub32), .in13(B), .in14(mulh32),
    .out(Result), .sel(ALUSel));  // open: in8, in9, in15

  // Other names for the same wires on the sheet: bsel32[31:0] = B

  // Notes on the sheet:
  //   INPUTS to your circuit
  //   DON'T CHANGE THE LOCATIONS OF THE INPUTS AND OUTPUTS!
  //   OUTPUT from your circuit
endmodule
