// Logisim project control_logic.circ as structural Verilog: 1 circuit, main circuit control_logic
module control_logic (
  input  [31:0] inst,
  input  BrEq,
  input  BrLt,
  output PCSel,
  output RegWEn,
  output [2:0] ImmSel,
  output BrUn,
  output ASel,
  output BSel,
  output [3:0] ALUSel,
  output MemRW,
  output [1:0] WBSel,
  output CSRSel,
  output CSRWen
);

  wire add, addi, and1, and_1_out, and_2_out, and_3_out, and_4_out, and_5_out, and_6_out, and_7_out,
       and_8_out, and_9_out, and_10_out, and_11_out, and_29_out, and_35_out, and_36_out, and_37_out,
       and_38_out, and_42_out, and_43_out, and_44_out, and_45_out, and_55_out, and_56_out, and_57_out, andi,
       auipc, beq, bge, bgeu, blt, bltu, bne, comparator_11_eq, comparator_12_eq, comparator_13_eq,
       comparator_14_eq, comparator_15_eq, comparator_16_eq, comparator_17_eq, comparator_18_eq,
       comparator_19_eq, comparator_20_eq, comparator_21_eq, comparator_22_eq, comparator_23_eq,
       comparator_24_eq, comparator_25_eq, comparator_26_eq, comparator_27_eq, comparator_28_eq,
       comparator_29_eq, comparator_30_eq, comparator_31_eq, comparator_32_eq, comparator_33_eq,
       comparator_34_eq, comparator_35_eq, comparator_36_eq, comparator_37_eq, comparator_38_eq,
       comparator_39_eq, comparator_40_eq, comparator_41_eq, comparator_42_eq, comparator_43_eq,
       comparator_44_eq, comparator_45_eq, comparator_46_eq, comparator_47_eq, comparator_48_eq,
       comparator_49_eq, comparator_50_eq, comparator_51_eq, comparator_52_eq, comparator_53_eq,
       comparator_54_eq, comparator_55_eq, comparator_56_eq, comparator_57_eq, comparator_58_eq, csrw, I_csr,
       I_Imm, I_jal, I_Loads, jal, jalr, lb, lh, lui, lw, mul, mulh, mulhu, not_1_out, not_2_out, not_3_out,
       or1, or_2_out, or_3_out, or_4_out, or_5_out, or_6_out, or_7_out, or_8_out, or_9_out, or_11_out,
       or_13_out, or_14_out, or_15_out, or_16_out, or_17_out, ori, R, SB, sb_t, sh, sll1, slli, slt, slti,
       sra1, srai, srl1, srli, sub, sw, U_Imm, U_Pc, UJ, xor1, xori;
  wire [1:0] branch_WBSel, mem_WBSel, reg_WBSel;
  wire [3:0] and_ALUSel, mul_ALUSel, mulh_ALUSel, mulhu_ALUSel, or_ALUSel, sll_ALUSel, slt_ALUSel,
       sra_ALUSel, srl_ALUSel, sub_ALUSel, xor_ALUSel;

  Multiplexer #(.enable("false"), .width(4)) multiplexer_1 (.in0(4'b0000), .in1(4'b1010), .out(mul_ALUSel), .sel(mul));
  Multiplexer #(.enable("false"), .width(4)) multiplexer_2 (.in0(4'b0000), .in1(4'b1100), .out(sub_ALUSel), .sel(sub));
  Comparator #(.width(7)) comparator_1 (.a(inst[6:0]), .b(7'b0110011), .eq(R));  // open: gt, lt
  Comparator #(.width(7)) comparator_2 (.a(inst[6:0]), .b(7'b0000011), .eq(I_Loads));  // open: gt, lt
  Comparator #(.width(7)) comparator_3 (.a(inst[6:0]), .b(7'b0010011), .eq(I_Imm));  // open: gt, lt
  Comparator #(.width(7)) comparator_4 (.a(inst[6:0]), .b(7'b0100011), .eq(MemRW));  // open: gt, lt
  Comparator #(.width(7)) comparator_5 (.a(inst[6:0]), .b(7'b1100011), .eq(SB));  // open: gt, lt
  Comparator #(.width(7)) comparator_6 (.a(inst[6:0]), .b(7'b0010111), .eq(U_Pc));  // open: gt, lt
  Comparator #(.width(7)) comparator_7 (.a(inst[6:0]), .b(7'b0110111), .eq(U_Imm));  // open: gt, lt
  Comparator #(.width(7)) comparator_8 (.a(inst[6:0]), .b(7'b1101111), .eq(UJ));  // open: gt, lt
  Comparator #(.width(7)) comparator_9 (.a(inst[6:0]), .b(7'b1100111), .eq(I_jal));  // open: gt, lt
  Comparator #(.width(7)) comparator_10 (.a(inst[6:0]), .b(7'b1110011), .eq(I_csr));  // open: gt, lt
  assign ALUSel = 4'b0000 | mul_ALUSel | sub_ALUSel | mulh_ALUSel | mulhu_ALUSel | slt_ALUSel | srl_ALUSel | sra_ALUSel | or_ALUSel | sll_ALUSel | and_ALUSel | xor_ALUSel;  // OR_Gate or_1, 4 bits wide
  Multiplexer #(.enable("false"), .width(4)) multiplexer_3 (
    .in0(4'b0000), .in1(4'b1110), .out(mulh_ALUSel), .sel(mulh));
  Multiplexer #(.enable("false"), .width(4)) multiplexer_4 (
    .in0(4'b0000), .in1(4'b1011), .out(mulhu_ALUSel), .sel(mulhu));
  Multiplexer #(.enable("false"), .width(4)) multiplexer_5 (
    .in0(4'b0000), .in1(4'b0111), .out(slt_ALUSel), .sel(or_2_out));
  or or_2 (or_2_out, slti, slt);
  and and_1 (and_1_out, R, 1'b1);
  and and_2 (and_2_out, I_Loads, 1'b1);
  and and_3 (and_3_out, I_csr, 1'b1);
  Multiplexer #(.enable("false"), .width(4)) multiplexer_6 (
    .in0(4'b0000), .in1(4'b0100), .out(srl_ALUSel), .sel(or_3_out));
  or or_3 (or_3_out, srl1, srli);
  Multiplexer #(.enable("false"), .width(4)) multiplexer_7 (
    .in0(4'b0000), .in1(4'b0101), .out(sra_ALUSel), .sel(or_4_out));
  or or_4 (or_4_out, sra1, srai);
  Multiplexer #(.enable("false"), .width(4)) multiplexer_8 (
    .in0(4'b0000), .in1(4'b0010), .out(or_ALUSel), .sel(or_5_out));
  or or_5 (or_5_out, or1, ori);
  Comparator #(.width(3)) comparator_11 (.a(inst[14:12]), .b(3'b000), .eq(comparator_11_eq));  // open: gt, lt
  Comparator #(.width(3)) comparator_12 (.a(inst[14:12]), .b(3'b001), .eq(comparator_12_eq));  // open: gt, lt
  Comparator #(.width(3)) comparator_13 (.a(inst[14:12]), .b(3'b011), .eq(comparator_13_eq));  // open: gt, lt
  Comparator #(.width(3)) comparator_14 (.a(inst[14:12]), .b(3'b010), .eq(comparator_14_eq));  // open: gt, lt
  Comparator #(.width(3)) comparator_15 (.a(inst[14:12]), .b(3'b100), .eq(comparator_15_eq));  // open: gt, lt
  Comparator #(.width(3)) comparator_16 (.a(inst[14:12]), .b(3'b101), .eq(comparator_16_eq));  // open: gt, lt
  Comparator #(.width(3)) comparator_17 (.a(inst[14:12]), .b(3'b110), .eq(comparator_17_eq));  // open: gt, lt
  Comparator #(.width(3)) comparator_18 (.a(inst[14:12]), .b(3'b111), .eq(comparator_18_eq));  // open: gt, lt
  Comparator #(.width(3)) comparator_19 (.a(inst[14:12]), .b(3'b000), .eq(comparator_19_eq));  // open: gt, lt
  Comparator #(.width(3)) comparator_20 (.a(inst[14:12]), .b(3'b001), .eq(comparator_20_eq));  // open: gt, lt
  Comparator #(.width(3)) comparator_21 (.a(inst[14:12]), .b(3'b010), .eq(comparator_21_eq));  // open: gt, lt
  Comparator #(.width(3)) comparator_22 (.a(inst[14:12]), .b(3'b001), .eq(comparator_22_eq));  // open: gt, lt
  Comparator #(.width(3)) comparator_23 (.a(inst[14:12]), .b(3'b101), .eq(comparator_23_eq));  // open: gt, lt
  and and_4 (and_4_out, and_1_out, comparator_11_eq);
  and and_5 (and_5_out, and_1_out, comparator_12_eq);
  and and_6 (and_6_out, and_1_out, comparator_13_eq);
  and and_7 (and_7_out, and_1_out, comparator_14_eq);
  and and_8 (and_8_out, and_1_out, comparator_15_eq);
  and and_9 (and_9_out, and_1_out, comparator_16_eq);
  and and_10 (and_10_out, and_1_out, comparator_17_eq);
  and and_11 (and_11_out, and_1_out, comparator_18_eq);
  and and_12 (lb, and_2_out, comparator_19_eq);
  and and_13 (lh, and_2_out, comparator_20_eq);
  and and_14 (lw, and_2_out, comparator_21_eq);
  and and_15 (csrw, and_3_out, comparator_22_eq);
  and and_16 (CSRSel, and_3_out, comparator_23_eq);
  Multiplexer #(.enable("false"), .width(4)) multiplexer_9 (
    .in0(4'b0000), .in1(4'b0110), .out(sll_ALUSel), .sel(or_6_out));
  or or_6 (or_6_out, sll1, slli);
  Multiplexer #(.enable("false"), .width(4)) multiplexer_10 (
    .in0(4'b0000), .in1(4'b0001), .out(and_ALUSel), .sel(or_7_out));
  or or_7 (or_7_out, and1, andi);
  Multiplexer #(.enable("false"), .width(4)) multiplexer_11 (
    .in0(4'b0000), .in1(4'b0011), .out(xor_ALUSel), .sel(or_8_out));
  or or_8 (or_8_out, xori, xor1);
  Comparator #(.width(7)) comparator_24 (.a(inst[31:25]), .b({7{1'b0}}), .eq(comparator_24_eq));  // open: gt, lt
  Comparator #(.width(7)) comparator_25 (.a(inst[31:25]), .b(7'b0000001), .eq(comparator_25_eq));  // open: gt, lt
  Comparator #(.width(7)) comparator_26 (.a(inst[31:25]), .b(7'b0100000), .eq(comparator_26_eq));  // open: gt, lt
  Comparator #(.width(7)) comparator_27 (.a(inst[31:25]), .b({7{1'b0}}), .eq(comparator_27_eq));  // open: gt, lt
  Comparator #(.width(7)) comparator_28 (.a(inst[31:25]), .b(7'b0000001), .eq(comparator_28_eq));  // open: gt, lt
  Comparator #(.width(7)) comparator_29 (.a(inst[31:25]), .b(7'b0000001), .eq(comparator_29_eq));  // open: gt, lt
  Comparator #(.width(7)) comparator_30 (.a(inst[31:25]), .b({7{1'b0}}), .eq(comparator_30_eq));  // open: gt, lt
  Comparator #(.width(7)) comparator_31 (.a(inst[31:25]), .b({7{1'b0}}), .eq(comparator_31_eq));  // open: gt, lt
  Comparator #(.width(7)) comparator_32 (.a(inst[31:25]), .b({7{1'b0}}), .eq(comparator_32_eq));  // open: gt, lt
  Comparator #(.width(7)) comparator_33 (.a(inst[31:25]), .b(7'b0100000), .eq(comparator_33_eq));  // open: gt, lt
  Comparator #(.width(7)) comparator_34 (.a(inst[31:25]), .b({7{1'b0}}), .eq(comparator_34_eq));  // open: gt, lt
  Comparator #(.width(7)) comparator_35 (.a(inst[31:25]), .b({7{1'b0}}), .eq(comparator_35_eq));  // open: gt, lt
  and and_17 (add, and_4_out, comparator_24_eq);
  and and_18 (mul, and_4_out, comparator_25_eq);
  and and_19 (sub, and_4_out, comparator_26_eq);
  and and_20 (sll1, and_5_out, comparator_27_eq);
  and and_21 (mulh, and_5_out, comparator_28_eq);
  and and_22 (mulhu, and_6_out, comparator_29_eq);
  and and_23 (slt, and_7_out, comparator_30_eq);
  and and_24 (xor1, and_8_out, comparator_31_eq);
  and and_25 (srl1, and_9_out, comparator_32_eq);
  and and_26 (sra1, and_9_out, comparator_33_eq);
  and and_27 (or1, and_10_out, comparator_34_eq);
  and and_28 (and1, and_11_out, comparator_35_eq);
  and and_29 (and_29_out, I_Imm, 1'b1);
  Comparator #(.width(3)) comparator_36 (.a(inst[14:12]), .b(3'b000), .eq(comparator_36_eq));  // open: gt, lt
  Comparator #(.width(3)) comparator_37 (.a(inst[14:12]), .b(3'b010), .eq(comparator_37_eq));  // open: gt, lt
  Comparator #(.width(3)) comparator_38 (.a(inst[14:12]), .b(3'b100), .eq(comparator_38_eq));  // open: gt, lt
  Comparator #(.width(3)) comparator_39 (.a(inst[14:12]), .b(3'b110), .eq(comparator_39_eq));  // open: gt, lt
  Comparator #(.width(3)) comparator_40 (.a(inst[14:12]), .b(3'b111), .eq(comparator_40_eq));  // open: gt, lt
  Comparator #(.width(3)) comparator_41 (.a(inst[14:12]), .b(3'b001), .eq(comparator_41_eq));  // open: gt, lt
  Comparator #(.width(3)) comparator_42 (.a(inst[14:12]), .b(3'b101), .eq(comparator_42_eq));  // open: gt, lt
  and and_30 (addi, and_29_out, comparator_36_eq);
  and and_31 (slti, and_29_out, comparator_37_eq);
  and and_32 (xori, and_29_out, comparator_38_eq);
  and and_33 (ori, and_29_out, comparator_39_eq);
  and and_34 (andi, and_29_out, comparator_40_eq);
  and and_35 (and_35_out, and_29_out, comparator_41_eq);
  and and_36 (and_36_out, and_29_out, comparator_42_eq);
  Comparator #(.width(7)) comparator_43 (.a(inst[31:25]), .b({7{1'b0}}), .eq(comparator_43_eq));  // open: gt, lt
  Comparator #(.width(7)) comparator_44 (.a(inst[31:25]), .b({7{1'b0}}), .eq(comparator_44_eq));  // open: gt, lt
  Comparator #(.width(7)) comparator_45 (.a(inst[31:25]), .b(7'b0100000), .eq(comparator_45_eq));  // open: gt, lt
  and and_37 (and_37_out, MemRW, 1'b1);
  and and_38 (and_38_out, SB, 1'b1);
  and and_39 (slli, and_35_out, comparator_43_eq);
  and and_40 (srli, and_36_out, comparator_44_eq);
  and and_41 (srai, and_36_out, comparator_45_eq);
  not not_1 (not_1_out, BrLt);
  or or_9 (or_9_out, bge, bgeu);
  or or_10 (BrUn, bltu, bgeu);
  or or_11 (or_11_out, blt, bltu);
  and and_42 (and_42_out, beq, BrEq);
  and and_43 (and_43_out, not_1_out, or_9_out);
  Comparator #(.width(3)) comparator_46 (.a(inst[14:12]), .b(3'b000), .eq(comparator_46_eq));  // open: gt, lt
  Comparator #(.width(3)) comparator_47 (.a(inst[14:12]), .b(3'b001), .eq(comparator_47_eq));  // open: gt, lt
  Comparator #(.width(3)) comparator_48 (.a(inst[14:12]), .b(3'b010), .eq(comparator_48_eq));  // open: gt, lt
  Comparator #(.width(3)) comparator_49 (.a(inst[14:12]), .b(3'b000), .eq(comparator_49_eq));  // open: gt, lt
  Comparator #(.width(3)) comparator_50 (.a(inst[14:12]), .b(3'b001), .eq(comparator_50_eq));  // open: gt, lt
  Comparator #(.width(3)) comparator_51 (.a(inst[14:12]), .b(3'b100), .eq(comparator_51_eq));  // open: gt, lt
  Comparator #(.width(3)) comparator_52 (.a(inst[14:12]), .b(3'b101), .eq(comparator_52_eq));  // open: gt, lt
  Comparator #(.width(3)) comparator_53 (.a(inst[14:12]), .b(3'b110), .eq(comparator_53_eq));  // open: gt, lt
  Comparator #(.width(3)) comparator_54 (.a(inst[14:12]), .b(3'b111), .eq(comparator_54_eq));  // open: gt, lt
  and and_44 (and_44_out, or_11_out, BrLt);
  and and_45 (and_45_out, and_43_out, BrEq);
  not not_2 (not_2_out, BrEq);
  and and_46 (sb_t, and_37_out, comparator_46_eq);
  and and_47 (sh, and_37_out, comparator_47_eq);
  and and_48 (sw, and_37_out, comparator_48_eq);
  and and_49 (beq, and_38_out, comparator_49_eq);
  and and_50 (bne, and_38_out, comparator_50_eq);
  and and_51 (blt, and_38_out, comparator_51_eq);
  and and_52 (bge, and_38_out, comparator_52_eq);
  and and_53 (bltu, and_38_out, comparator_53_eq);
  and and_54 (bgeu, and_38_out, comparator_54_eq);
  or or_12 (PCSel, and_45_out, and_42_out, and_44_out, jalr, jal, and_55_out);
  and and_55 (and_55_out, not_2_out, bne);
  and and_56 (and_56_out, I_jal, 1'b1);
  and and_57 (and_57_out, I_csr, 1'b1);
  and and_58 (auipc, U_Pc, 1'b1);
  and and_59 (lui, U_Imm, 1'b1);
  and and_60 (jal, UJ, 1'b1);
  or or_13 (or_13_out, R, I_Loads, I_Imm, U_Pc, U_Imm, UJ, I_jal);
  or or_14 (or_14_out, R, I_Imm, U_Pc, U_Imm);
  Multiplexer #(.enable("false"), .width(2)) multiplexer_12 (.in0(2'b00), .in1(2'b00), .out(mem_WBSel), .sel(I_Loads));
  or or_15 (or_15_out, I_jal, UJ);
  or or_16 (or_16_out, I_Loads, I_Imm, I_jal);
  or or_17 (or_17_out, U_Pc, U_Imm);
  Comparator #(.width(3)) comparator_55 (.a(inst[14:12]), .b(3'b000), .eq(comparator_55_eq));  // open: gt, lt
  Comparator #(.width(3)) comparator_56 (.a(inst[14:12]), .b(3'b001), .eq(comparator_56_eq));  // open: gt, lt
  Comparator #(.width(3)) comparator_57 (.a(inst[14:12]), .b(3'b101), .eq(comparator_57_eq));  // open: gt, lt
  not not_3 (not_3_out, comparator_58_eq);
  Comparator #(.width(5)) comparator_58 (.a(inst[11:7]), .b({5{1'b0}}), .eq(comparator_58_eq));  // open: gt, lt
  or or_18 (ASel, SB, UJ, U_Pc);
  or or_19 (BSel, SB, MemRW, U_Pc, U_Imm, I_jal, UJ, I_Loads, I_Imm);
  or or_20 (CSRWen, csrw, CSRSel);
  Multiplexer #(.enable("false"), .width(2)) multiplexer_13 (
    .in0(2'b00), .in1(2'b01), .out(reg_WBSel), .sel(or_14_out));
  Multiplexer #(.enable("false"), .width(2)) multiplexer_14 (
    .in0(2'b00), .in1(2'b10), .out(branch_WBSel), .sel(or_15_out));
  assign WBSel = reg_WBSel | mem_WBSel | branch_WBSel;  // OR_Gate or_21, 2 bits wide
  Priority_Encoder priority_encoder_1 (
    .in0(R), .in1(or_16_out), .in2(MemRW), .in3(SB), .in4(or_17_out), .in5(UJ), .in6(I_csr), .out(ImmSel));  // open: in7, en_in, gs, en_out
  and and_61 (jalr, and_56_out, comparator_55_eq);
  and and_62 (csrw, and_57_out, comparator_56_eq);
  and and_63 (CSRSel, and_57_out, comparator_57_eq);
  and and_64 (RegWEn, or_13_out, not_3_out);

  // Other names for the same wires on the sheet: csrwi = CSRSel; opcode[6:0] = inst[6:0]; rd[4:0] = inst[11:7];
  //   funct3[2:0] = inst[14:12]; funct7[6:0] = inst[31:25]; S = MemRW

  // Notes on the sheet:
  //   INPUTS to your circuit
  //   ALUSel
  //   R Type
  //   I Type
  //   I Type
  //   S Type
  //   SB Type
  //   U Type
  //   U Type
  //   UJ Type
  //   I Type
  //   I Type
  //   DON'T CHANGE THE LOCATIONS OF THE INPUTS AND OUTPUTS!
  //   OUTPUT from your circuit
endmodule
