// Logisim project cpu.circ as structural Verilog: 1 circuit, main circuit cpu
module cpu (
  input  clk,
  input  [31:0] INSTRUCTION,
  input  [31:0] READ_DATA,
  output [31:0] WRITE_ADDRESS,
  output [31:0] PROGRAM_COUNTER,
  output [31:0] ra,
  output [31:0] sp,
  output [31:0] t0,
  output [31:0] t1,
  output [31:0] t2,
  output [31:0] s0,
  output [31:0] s1,
  output [31:0] a0,
  output [31:0] tohost,
  output [3:0] WRITE_ENABLE,
  output [31:0] WRITE_DATA
);

  wire ASel, BrEq, BrLt, BrUn, BSel, control_logic_1_memrw, CSRSel, CSRWen, or_1_out, PCSel, RegWEn;
  wire [1:0] WBSel;
  wire [2:0] funct3, ImmSel;
  wire [3:0] ALUSel;
  wire [6:0] funct7;
  wire [24:0] INSTRUCTION_pipeline;
  wire [31:0] adder_1_out, adder_2_out, AluA, AluB, Areg, imm, multiplexer_1_out, multiplexer_2_out,
       PROGRAM_COUNTER_pipeline, WriteReg;

  Adder #(.width(32)) adder_1 (.a(PROGRAM_COUNTER), .b(32'h4), .out(adder_1_out));  // open: cin, cout
  Multiplexer #(.enable("false"), .width(32)) multiplexer_1 (
    .in0(adder_1_out), .in1(WRITE_ADDRESS), .out(multiplexer_1_out), .sel(PCSel));
  Register #(.width(32)) PC (.D(multiplexer_1_out), .clk(clk), .Q(PROGRAM_COUNTER));  // open: en, clr
  Register #(.width(32)) PCReg (.D(PROGRAM_COUNTER), .clk(clk), .Q(PROGRAM_COUNTER_pipeline));  // open: en, clr
  Multiplexer #(.enable("false"), .width(32)) multiplexer_2 (
    .in0(INSTRUCTION), .in1(32'h13), .out(multiplexer_2_out), .sel(PCSel));
  Register #(.width(32)) InstReg (
    .D(multiplexer_2_out), .clk(clk),
    .Q({funct7, INSTRUCTION_pipeline[24:15], funct3, INSTRUCTION_pipeline[11:0]}));  // open: en, clr
  imm_gen imm_gen_1 (
    .inst({funct7, INSTRUCTION_pipeline[24:15], funct3, INSTRUCTION_pipeline[11:0]}), .ImmSel(ImmSel),
    .imm(imm));
  control_logic control_logic_1 (
    .CSRWen(CSRWen), .PCSel(PCSel), .RegWEn(RegWEn), .ImmSel(ImmSel), .BrUn(BrUn), .ASel(ASel), .BSel(BSel),
    .ALUSel(ALUSel), .MemRW(control_logic_1_memrw), .WBSel(WBSel), .CSRSel(CSRSel),
    .inst({funct7, INSTRUCTION_pipeline[24:15], funct3, INSTRUCTION_pipeline[11:0]}), .BrEq(BrEq), .BrLt(BrLt));
  Multiplexer #(.enable("false"), .width(32)) multiplexer_3 (.in0(WRITE_DATA), .in1(imm), .out(AluB), .sel(or_1_out));
  or or_1 (or_1_out, BSel, CSRSel);
  Multiplexer #(.enable("false"), .width(32)) multiplexer_4 (
    .in0(Areg), .in1(PROGRAM_COUNTER_pipeline), .out(AluA), .sel(ASel));
  regfile regfile_1 (
    .rs1(INSTRUCTION_pipeline[19:15]), .rs2(INSTRUCTION_pipeline[24:20]), .rd(INSTRUCTION_pipeline[11:7]),
    .Write_Data(WriteReg), .RegWEn(RegWEn), .clk(clk), .ra(ra), .sp(sp), .t0(t0), .t1(t1), .t2(t2), .s0(s0),
    .s1(s1), .a0(a0), .Read_Data_1(Areg), .Read_Data_2(WRITE_DATA));
  branch_comp branch_comp_1 (.rs1(Areg), .rs2(WRITE_DATA), .BrUn(BrUn), .BrEq(BrEq), .BrLt(BrLt));
  assign WRITE_ENABLE = {{3{control_logic_1_memrw}}, control_logic_1_memrw};  // Bit_Extender bit_extender_1
  Adder #(.width(32)) adder_2 (.a(32'h4), .b(PROGRAM_COUNTER_pipeline), .out(adder_2_out));  // open: cin, cout
  Multiplexer #(.enable("false"), .select(2), .width(32)) multiplexer_5 (
    .in0(READ_DATA), .in1(WRITE_ADDRESS), .in2(adder_2_out), .out(WriteReg), .sel(WBSel));  // open: in3
  alu alu_1 (.Result(WRITE_ADDRESS), .A(AluA), .B(AluB), .ALUSel(ALUSel));
  csr csr_1 (.CSR_address(12'h51e), .CSR_din(WRITE_ADDRESS), .CSR_WE(CSRWen), .clk(clk), .tohost(tohost));

  // Other names for the same wires on the sheet: ALURes[31:0] = WRITE_ADDRESS; Breg[31:0] = WRITE_DATA;
  //   opcode[6:0] = INSTRUCTION_pipeline[6:0]; rd[4:0] = INSTRUCTION_pipeline[11:7];
  //   INSTRUCTION_pipeline (some bits) = {funct7, funct3}; rs1[4:0] = INSTRUCTION_pipeline[19:15];
  //   rs2[4:0] = INSTRUCTION_pipeline[24:20]

  // Notes on the sheet:
  //   Output to IMEM
  //   IMEM (do **NOT** move this)
  //   Inputs from IMEM
  //   It is OK to move the PC, RegFile, ALU, MEM, Branch Comp, Imm Gen, and Control Logic to wherever is most convenient for you when constructing your CPU, and to delete this text
  //   Control Unit
  //   Inputs/Outputs for testing. Do **NOT** move these.
  //   PC + 4
  //   WRITE_ENABLE 4bit choose whick block memory read/write but MemRW is 0, mean passive read , trigger one read operation or not? hopefuly not  
  //   Outputs To DMEM
  //   DMEM (do **NOT** move this)
  //   Inputs From DMEM
endmodule
